# Fritzing sketch rocket-lamp (saved by Fritzing 0.9.4)

parts:
  U1 = POT [package=pot_mammoth]
  S1 = Round Pushbutton
  U2 = WS2812 RGB LED strip
  Pico/Pico2_Mod_1 = Raspberry Pi Pico or Pico 2
  JACK1 = 2.1mm Barrel Jack with Terminal Block

nets:
  N1: U1.S, S1.leg0, Pico/Pico2_Mod_1.pin_35
  N2: U1.A, Pico/Pico2_Mod_1.pin_31
  N3: U1.E, U2.GND, Pico/Pico2_Mod_1.pin_3, Pico/Pico2_Mod_1.pin_33, Pico/Pico2_Mod_1.pin_38, Pico/Pico2_Mod_1.pin_42, JACK1.NEG
  N4: S1.leg1, Pico/Pico2_Mod_1.pin_22
  N5: U2.VCC, Pico/Pico2_Mod_1.pin_39, JACK1.POS
  N6: U2.DIN, Pico/Pico2_Mod_1.pin_29

notes:
  GP17
  GP22
  GP26
  AGND
  ADC_VREF

custom parts:
  WS2812 RGB LED strip: WS2812 strip
  Raspberry Pi Pico or Pico 2: Raspberry Pi Pico and Pico 2. Based around the RP2040 and RP2350 microcontrollers respectively, Picos are low cost microcontroller device bringing Raspberry Pi quality, cost, and easy of use to the microcontroller space. Jan 2021, Split part in to two versions: tht (this one) and SMD. This one will drill holes for a .1 in header in pcb to allow plugging in the module as well as providing pads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
